# Fritzing sketch HalloweenLEDs (saved by Fritzing 0.9.3b)

parts:
  Componente1 = Arduino Nano (Rev3.0) (ICSP)
  LED1 = LED - 5mm [color="Yellow (595nm)" package="5 mm [THT]"]
  LED2 = LED - 5mm [color="Yellow (595nm)" package="5 mm [THT]"]
  LED3 = LED - 5mm [color="Yellow (595nm)" package="5 mm [THT]"]
  LED4 = LED - 5mm [color="Yellow (595nm)" package="5 mm [THT]"]
  LED5 = LED - 5mm [color="Yellow (595nm)" package="5 mm [THT]"]
  R1 = Resistor [tolerance=±5% resistance=220 package=THT]
  R2 = Resistor [tolerance=±5% resistance=220 package=THT]
  R3 = Resistor [tolerance=±5% resistance=220 package=THT]
  R4 = Resistor [tolerance=±5% resistance=220 package=THT]
  R5 = Resistor [tolerance=±5% resistance=220 package=THT]
  VCC1 = Battery block 9V

nets:
  N1: Componente1.GND, LED3.cathode, VCC1.-
  N2: Componente1.D5, R3.Pin_0, R4.Pin_0, R5.Pin_0
  N3: Componente1.D6, R1.Pin_0, R2.Pin_0
  N4: Componente1.VIN, VCC1.+
  N5: LED1.cathode, LED2.cathode, LED4.cathode, LED5.cathode
  N6: LED1.anode, R1.Pin_1
  N7: LED2.anode, R2.Pin_1
  N8: LED3.anode, R5.Pin_1
  N9: LED4.anode, R4.Pin_1
  N10: LED5.anode, R3.Pin_1

notes:
  eyes
  mouth
